# Fritzing sketch circuito (saved by Fritzing 1.0.0rc)
breadboards: 2

parts:
  LCD2 = LCD screen
  LCM1602_IIC2 = LCM1602 IIC [part_number="LCM1602 IIC" chip_label="LCM1602 IIC" package="DIP (Dual Inline) [THT]"]
  SD_card_module2 = SD Card Module
  S1 = Round Pushbutton
  S2 = Round Pushbutton
  S3 = Round Pushbutton
  S4 = Round Pushbutton
  S5 = Round Pushbutton
  R1 = Resistor [tolerance=±5% resistance=220 package="2512 [SMD]"]
  R2 = Resistor [tolerance=±5% resistance=220 package="2512 [SMD]"]
  R3 = Resistor [tolerance=±5% resistance=220 package="2512 [SMD]"]
  R4 = Resistor [tolerance=±5% resistance=220 package="2512 [SMD]"]
  R5 = Resistor [tolerance=±5% resistance=220 package="2512 [SMD]"]
  Componente3 = Arduino Nano (Rev3.0)
  Componente2 = RFID-RC522-v2

nets:
  VSS: LCD2.VSS, LCM1602_IIC2.VSS
  VDD: LCD2.VDD, LCM1602_IIC2.VDD
  N1: LCD2.V0, LCM1602_IIC2.V0
  N2: LCD2.RS, LCM1602_IIC2.RS
  N3: LCD2.R/W, LCM1602_IIC2.RW
  N4: LCD2.E, LCM1602_IIC2.E
  N5: LCD2.DB0, LCM1602_IIC2.D0
  N6: LCD2.DB1, LCM1602_IIC2.D1
  N7: LCD2.DB2, LCM1602_IIC2.D2
  N8: LCD2.DB3, LCM1602_IIC2.D3
  N9: LCD2.DB4, LCM1602_IIC2.D4
  N10: LCD2.DB5, LCM1602_IIC2.D5
  N11: LCD2.DB6, LCM1602_IIC2.D6
  N12: LCD2.DB7, LCM1602_IIC2.D7
  N13: LCD2.LED+, LCM1602_IIC2.A
  N14: LCD2.LED-, LCM1602_IIC2.K
  GND: LCM1602_IIC2.GND, SD_card_module2.GND, Componente3.GND, Componente2.GND
  VCC: LCM1602_IIC2.VCC, Componente3.5V
  N15: LCM1602_IIC2.SDA, Componente3.A4
  N16: LCM1602_IIC2.SCL, Componente3.A5
  N17: LCM1602_IIC2.LED_A, LCM1602_IIC2.LED_B
  N18: SD_card_module2.+3.3, Componente3.3V3, Componente2.3_3V
  N19: SD_card_module2.CS, Componente3.D4
  N20: SD_card_module2.MOSI, Componente3.D11/MOSI, Componente2.MOSI
  N21: SD_card_module2.SCK, Componente3.D13/SCK, Componente2.SCK
  N22: SD_card_module2.MISO, Componente3.D12/MISO, Componente2.MISO
  N23: S1.leg0, R1.Pin_1
  N24: S1.leg1, S2.leg1, S3.leg1, S4.leg1, S5.leg1
  N25: S2.leg0, R2.Pin_1
  N26: S3.leg0, R3.Pin_1
  N27: S4.leg0, R4.Pin_1
  N28: S5.leg0, R5.Pin_1
  N29: R1.Pin_0, R2.Pin_0, R3.Pin_0, R4.Pin_0, R5.Pin_0
  N30: Componente3.D9, Componente2.RST
  N31: Componente3.D10, Componente2.SDA

custom parts:
  LCM1602 IIC: I2C-Module to use a 1602 or 2004 LCD on with the wire.h libory Serial LCD Modul
  SD Card Module: SD Card Module Slot Socket Reader For Arduino ARM MCU
  RFID-RC522-v2: A simple China made RFID-RC522 Reader; do check the pin labels, as this is a MFRC522 based clone.
